// Logisim project e2476844.circ as structural Verilog: 1 circuit, main circuit main
module main (
  input  O3,
  input  O2,
  input  O1,
  input  O0,
  input  A1,
  input  A0,
  input  B1,
  input  B0,
  output L7,
  output L8,
  output L9,
  output L5,
  output L6,
  output E,
  output G,
  output L,
  output S,
  output C,
  output Z,
  output P,
  output L0,
  output L1,
  output L2,
  output L3,
  output L4
);

  wire n3_to_8_decoder_74138_1_p7, n3_to_8_decoder_74138_1_p8, n3_to_8_decoder_74138_1_p9,
       n3_to_8_decoder_74138_1_p10, n3_to_8_decoder_74138_1_p11, n3_to_8_decoder_74138_1_p12,
       n3_to_8_decoder_74138_1_p13, n3_to_8_decoder_74138_1_p14, n3_to_8_decoder_74138_2_p7, not_1_out,
       not_2_out, not_3_out, not_4_out, not_5_out, not_6_out, not_7_out, not_8_out, not_9_out, not_10_out,
       not_11_out, not_12_out, not_13_out, not_14_out, not_15_out, not_16_out, not_17_out, not_18_out,
       not_19_out, not_20_out, not_21_out, not_22_out, not_23_out, not_24_out, not_25_out, not_26_out,
       not_27_out, not_28_out, not_29_out, not_30_out, not_31_out, not_32_out, not_33_out, not_35_out,
       not_36_out, not_37_out, not_38_out, not_39_out, not_40_out, not_41_out, not_42_out, not_43_out,
       not_44_out, not_45_out, not_46_out, not_47_out, not_48_out, not_49_out, not_50_out, not_51_out,
       not_52_out, not_53_out, not_54_out, not_55_out, not_56_out, not_57_out, not_58_out, not_59_out,
       not_60_out, not_61_out, not_62_out, not_63_out, not_64_out, not_65_out, not_66_out, not_67_out,
       not_68_out, not_69_out, not_70_out, not_71_out, not_72_out, not_73_out, not_74_out, not_75_out,
       not_76_out, not_77_out, not_78_out, not_79_out, not_80_out, not_81_out, not_82_out, not_83_out,
       not_84_out, not_85_out, not_86_out, not_87_out, not_88_out, not_89_out, not_90_out, not_91_out,
       not_92_out, not_93_out, not_94_out, not_95_out, not_96_out, not_97_out, not_98_out, not_99_out,
       not_100_out, not_101_out, not_102_out, not_103_out, not_104_out, not_105_out, not_106_out,
       not_107_out, not_108_out, not_109_out, not_110_out, not_111_out, not_112_out, not_113_out,
       not_114_out, not_115_out, not_116_out, not_117_out, not_118_out, not_119_out, not_120_out,
       not_121_out, not_122_out, not_123_out, not_124_out, not_125_out, not_126_out, not_127_out,
       not_128_out, not_129_out, not_130_out, not_131_out, not_132_out, not_133_out, not_134_out,
       not_135_out, not_136_out, not_137_out, not_138_out, not_139_out, not_140_out, not_141_out,
       not_142_out, not_143_out, not_144_out, not_145_out, not_146_out, or_1_out, or_2_out, or_3_out,
       or_4_out, or_5_out, or_6_out, or_7_out, or_8_out, or_9_out, or_10_out, or_11_out, or_12_out,
       or_13_out, or_14_out, or_15_out, or_16_out, or_17_out, or_19_out, or_20_out, or_21_out, or_22_out,
       or_23_out, or_24_out, or_25_out, or_26_out, or_27_out, or_28_out, or_29_out, or_30_out, or_31_out,
       or_32_out, or_33_out, or_34_out, or_35_out, or_36_out, or_37_out, or_38_out, or_39_out, or_40_out,
       or_41_out, or_42_out, or_43_out, or_44_out, or_45_out, or_46_out, or_47_out, or_48_out, or_49_out,
       or_50_out, or_51_out, or_52_out, or_53_out, or_54_out, or_55_out, or_56_out, or_57_out, or_58_out,
       or_59_out, or_60_out, or_61_out, or_62_out, or_63_out, or_65_out, or_66_out, or_67_out, or_68_out,
       or_69_out, or_70_out, or_71_out, or_72_out, or_73_out, or_74_out, or_75_out, or_76_out, or_77_out,
       or_78_out, or_79_out, or_80_out, or_82_out, or_83_out, or_84_out, or_85_out, or_86_out, or_87_out,
       or_89_out, or_90_out, or_91_out, or_92_out, or_93_out, or_94_out, or_95_out, or_96_out, or_97_out,
       or_98_out, or_99_out, or_100_out, or_101_out, or_102_out, or_103_out, or_104_out, or_105_out,
       or_106_out, or_107_out, or_109_out, or_110_out, or_111_out, or_112_out, or_113_out, or_114_out,
       or_115_out, or_116_out, or_117_out, or_118_out, or_119_out, or_120_out, or_121_out, or_122_out,
       or_123_out, or_124_out, or_125_out, or_126_out, or_127_out, or_128_out, or_129_out, or_130_out,
       or_131_out, or_132_out, or_133_out, or_134_out, or_135_out, or_136_out, or_137_out, or_138_out,
       or_139_out, or_140_out, or_141_out, or_142_out, or_143_out, or_144_out, or_145_out, or_146_out,
       or_147_out, or_148_out, or_149_out, or_150_out, or_151_out, or_152_out, or_153_out, or_154_out,
       or_155_out, or_156_out, or_157_out, or_158_out, or_159_out, or_160_out, or_161_out, or_162_out,
       or_163_out, or_164_out, or_165_out, or_166_out, or_167_out, or_168_out, or_169_out, or_170_out,
       or_171_out, or_172_out, or_173_out, or_174_out, or_175_out, or_176_out, or_177_out, or_178_out,
       or_180_out, or_181_out, or_182_out, or_183_out, or_184_out, or_185_out, or_186_out, or_188_out,
       or_189_out, or_190_out, or_191_out, or_192_out, or_193_out, or_195_out, or_196_out, or_197_out,
       or_198_out, or_199_out, or_200_out, or_202_out, or_203_out, or_204_out, or_205_out, or_206_out,
       or_208_out, or_209_out, or_210_out, or_211_out, or_212_out, or_214_out, or_215_out, or_216_out,
       or_217_out, or_218_out, or_219_out, or_220_out;

  not not_1 (not_1_out, O3);
  // _3_to_8_decoder__74138 #(.Facing("east")) 3_to_8_decoder_74138_1: pin names not known; wires that end beside it: O0, O1, O2, not_1_out, 1'b0, 1'b0, n3_to_8_decoder_74138_1_p7, n3_to_8_decoder_74138_1_p8, n3_to_8_decoder_74138_1_p9, n3_to_8_decoder_74138_1_p10, n3_to_8_decoder_74138_1_p11, n3_to_8_decoder_74138_1_p12, n3_to_8_decoder_74138_1_p13, n3_to_8_decoder_74138_1_p14
  // _3_to_8_decoder__74138 #(.Facing("east")) 3_to_8_decoder_74138_2: pin names not known; wires that end beside it: O0, O1, O2, O3, 1'b0, 1'b0, n3_to_8_decoder_74138_2_p7
  not not_2 (not_2_out, A1);
  // _3_to_8_decoder__74138 #(.Facing("east")) 3_to_8_decoder_74138_3: pin names not known; wires that end beside it: B0, B1, A0
  // _3_to_8_decoder__74138 #(.Facing("east")) 3_to_8_decoder_74138_4: pin names not known; wires that end beside it: B0, B1, A0, not_2_out, A1, n3_to_8_decoder_74138_1_p7, n3_to_8_decoder_74138_1_p7, n3_to_8_decoder_74138_1_p7, n3_to_8_decoder_74138_1_p7
  // _3_to_8_decoder__74138 #(.Facing("east")) 3_to_8_decoder_74138_5: pin names not known; wires that end beside it: B0, B1, A0
  // _3_to_8_decoder__74138 #(.Facing("east")) 3_to_8_decoder_74138_6: pin names not known; wires that end beside it: B0, B1, A0, not_2_out, A1, n3_to_8_decoder_74138_1_p8, n3_to_8_decoder_74138_1_p8, n3_to_8_decoder_74138_1_p8, n3_to_8_decoder_74138_1_p8
  // _3_to_8_decoder__74138 #(.Facing("east")) 3_to_8_decoder_74138_7: pin names not known; wires that end beside it: B0, B1, A0
  // _3_to_8_decoder__74138 #(.Facing("east")) 3_to_8_decoder_74138_8: pin names not known; wires that end beside it: B0, B1, A0, not_2_out, A1, n3_to_8_decoder_74138_1_p12, n3_to_8_decoder_74138_1_p12, n3_to_8_decoder_74138_1_p12, n3_to_8_decoder_74138_1_p12
  // _3_to_8_decoder__74138 #(.Facing("east")) 3_to_8_decoder_74138_9: pin names not known; wires that end beside it: B0, B1, A0
  // _3_to_8_decoder__74138 #(.Facing("east")) 3_to_8_decoder_74138_10: pin names not known; wires that end beside it: B0, B1, A0, not_2_out, A1, n3_to_8_decoder_74138_1_p13, n3_to_8_decoder_74138_1_p13, n3_to_8_decoder_74138_1_p13, n3_to_8_decoder_74138_1_p13
  // _3_to_8_decoder__74138 #(.Facing("east")) 3_to_8_decoder_74138_11: pin names not known; wires that end beside it: B0, B1, A0
  // _3_to_8_decoder__74138 #(.Facing("east")) 3_to_8_decoder_74138_12: pin names not known; wires that end beside it: B0, B1, A0, not_2_out, A1, n3_to_8_decoder_74138_1_p14, n3_to_8_decoder_74138_1_p14, n3_to_8_decoder_74138_1_p14, n3_to_8_decoder_74138_1_p14
  // _3_to_8_decoder__74138 #(.Facing("east")) 3_to_8_decoder_74138_13: pin names not known; wires that end beside it: B0, B1, A0
  // _3_to_8_decoder__74138 #(.Facing("east")) 3_to_8_decoder_74138_14: pin names not known; wires that end beside it: B0, B1, A0, not_2_out, A1, n3_to_8_decoder_74138_2_p7, n3_to_8_decoder_74138_2_p7, n3_to_8_decoder_74138_2_p7, n3_to_8_decoder_74138_2_p7
  // NOT_Gate not_3 has open pins: in=open, out=not_3_out
  // NOT_Gate not_4 has open pins: in=open, out=not_4_out
  // NOT_Gate not_5 has open pins: in=open, out=not_5_out
  // NOT_Gate not_6 has open pins: in=open, out=not_6_out
  // NOT_Gate not_7 has open pins: in=open, out=not_7_out
  // NOT_Gate not_8 has open pins: in=open, out=not_8_out
  // NOT_Gate not_9 has open pins: in=open, out=not_9_out
  // NOT_Gate not_10 has open pins: in=open, out=not_10_out
  // NOT_Gate not_11 has open pins: in=open, out=not_11_out
  // NOT_Gate not_12 has open pins: in=open, out=not_12_out
  // NOT_Gate not_13 has open pins: in=open, out=not_13_out
  // NOT_Gate not_14 has open pins: in=open, out=not_14_out
  // NOT_Gate not_15 has open pins: in=open, out=not_15_out
  // NOT_Gate not_16 has open pins: in=open, out=not_16_out
  // NOT_Gate not_17 has open pins: in=open, out=not_17_out
  // NOT_Gate not_18 has open pins: in=open, out=not_18_out
  // _3_to_8_decoder__74138 #(.Facing("east")) 3_to_8_decoder_74138_15: pin names not known; wires that end beside it: B0, B1, A0
  // _3_to_8_decoder__74138 #(.Facing("east")) 3_to_8_decoder_74138_16: pin names not known; wires that end beside it: B0, B1, A0, not_2_out, A1, n3_to_8_decoder_74138_1_p9, n3_to_8_decoder_74138_1_p9, n3_to_8_decoder_74138_1_p9, n3_to_8_decoder_74138_1_p9
  // _3_to_8_decoder__74138 #(.Facing("east")) 3_to_8_decoder_74138_17: pin names not known; wires that end beside it: B0, B1, A0
  // _3_to_8_decoder__74138 #(.Facing("east")) 3_to_8_decoder_74138_18: pin names not known; wires that end beside it: B0, B1, A0, not_2_out, A1, n3_to_8_decoder_74138_1_p10, n3_to_8_decoder_74138_1_p10, n3_to_8_decoder_74138_1_p10, n3_to_8_decoder_74138_1_p10
  // _3_to_8_decoder__74138 #(.Facing("east")) 3_to_8_decoder_74138_19: pin names not known; wires that end beside it: B0, B1, A0
  // _3_to_8_decoder__74138 #(.Facing("east")) 3_to_8_decoder_74138_20: pin names not known; wires that end beside it: B0, B1, A0, not_2_out, A1, n3_to_8_decoder_74138_1_p11, n3_to_8_decoder_74138_1_p11, n3_to_8_decoder_74138_1_p11, n3_to_8_decoder_74138_1_p11
  or or_1 (or_1_out, not_4_out, not_5_out);
  or or_2 (or_2_out, not_6_out, not_8_out);
  or or_3 (or_3_out, or_1_out, or_2_out);
  or or_4 (or_4_out, or_3_out, or_29_out);
  // NOT_Gate not_19 has open pins: in=open, out=not_19_out
  // NOT_Gate not_20 has open pins: in=open, out=not_20_out
  // NOT_Gate not_21 has open pins: in=open, out=not_21_out
  // NOT_Gate not_22 has open pins: in=open, out=not_22_out
  // NOT_Gate not_23 has open pins: in=open, out=not_23_out
  // NOT_Gate not_24 has open pins: in=open, out=not_24_out
  // NOT_Gate not_25 has open pins: in=open, out=not_25_out
  // NOT_Gate not_26 has open pins: in=open, out=not_26_out
  // NOT_Gate not_27 has open pins: in=open, out=not_27_out
  // NOT_Gate not_28 has open pins: in=open, out=not_28_out
  // NOT_Gate not_29 has open pins: in=open, out=not_29_out
  // NOT_Gate not_30 has open pins: in=open, out=not_30_out
  // NOT_Gate not_31 has open pins: in=open, out=not_31_out
  // NOT_Gate not_32 has open pins: in=open, out=not_32_out
  // NOT_Gate not_33 has open pins: in=open, out=not_33_out
  // NOT_Gate not_34 has open pins: in=open, out=L9
  or or_5 (or_5_out, not_19_out, not_20_out);
  or or_6 (or_6_out, not_21_out, not_22_out);
  or or_7 (or_7_out, or_5_out, or_6_out);
  or or_8 (or_8_out, or_7_out, or_31_out);
  // NOT_Gate not_35 has open pins: in=open, out=not_35_out
  // NOT_Gate not_36 has open pins: in=open, out=not_36_out
  // NOT_Gate not_37 has open pins: in=open, out=not_37_out
  // NOT_Gate not_38 has open pins: in=open, out=not_38_out
  // NOT_Gate not_39 has open pins: in=open, out=not_39_out
  // NOT_Gate not_40 has open pins: in=open, out=not_40_out
  // NOT_Gate not_41 has open pins: in=open, out=not_41_out
  // NOT_Gate not_42 has open pins: in=open, out=not_42_out
  // NOT_Gate not_43 has open pins: in=open, out=not_43_out
  // NOT_Gate not_44 has open pins: in=open, out=not_44_out
  // NOT_Gate not_45 has open pins: in=open, out=not_45_out
  // NOT_Gate not_46 has open pins: in=open, out=not_46_out
  // NOT_Gate not_47 has open pins: in=open, out=not_47_out
  // NOT_Gate not_48 has open pins: in=open, out=not_48_out
  // NOT_Gate not_49 has open pins: in=open, out=not_49_out
  // NOT_Gate not_50 has open pins: in=open, out=not_50_out
  or or_9 (or_9_out, not_36_out, not_37_out);
  or or_10 (or_10_out, not_38_out, not_41_out);
  or or_11 (or_11_out, or_9_out, or_10_out);
  // NOT_Gate not_51 has open pins: in=open, out=not_51_out
  // NOT_Gate not_52 has open pins: in=open, out=not_52_out
  // NOT_Gate not_53 has open pins: in=open, out=not_53_out
  // NOT_Gate not_54 has open pins: in=open, out=not_54_out
  // NOT_Gate not_55 has open pins: in=open, out=not_55_out
  // NOT_Gate not_56 has open pins: in=open, out=not_56_out
  // NOT_Gate not_57 has open pins: in=open, out=not_57_out
  // NOT_Gate not_58 has open pins: in=open, out=not_58_out
  // NOT_Gate not_59 has open pins: in=open, out=not_59_out
  // NOT_Gate not_60 has open pins: in=open, out=not_60_out
  // NOT_Gate not_61 has open pins: in=open, out=not_61_out
  // NOT_Gate not_62 has open pins: in=open, out=not_62_out
  // NOT_Gate not_63 has open pins: in=open, out=not_63_out
  // NOT_Gate not_64 has open pins: in=open, out=not_64_out
  // NOT_Gate not_65 has open pins: in=open, out=not_65_out
  // NOT_Gate not_66 has open pins: in=open, out=not_66_out
  or or_12 (or_12_out, not_52_out, not_55_out);
  // NOT_Gate not_67 has open pins: in=open, out=not_67_out
  // NOT_Gate not_68 has open pins: in=open, out=not_68_out
  // NOT_Gate not_69 has open pins: in=open, out=not_69_out
  // NOT_Gate not_70 has open pins: in=open, out=not_70_out
  // NOT_Gate not_71 has open pins: in=open, out=not_71_out
  // NOT_Gate not_72 has open pins: in=open, out=not_72_out
  // NOT_Gate not_73 has open pins: in=open, out=not_73_out
  // NOT_Gate not_74 has open pins: in=open, out=not_74_out
  // NOT_Gate not_75 has open pins: in=open, out=not_75_out
  // NOT_Gate not_76 has open pins: in=open, out=not_76_out
  // NOT_Gate not_77 has open pins: in=open, out=not_77_out
  // NOT_Gate not_78 has open pins: in=open, out=not_78_out
  // NOT_Gate not_79 has open pins: in=open, out=not_79_out
  // NOT_Gate not_80 has open pins: in=open, out=not_80_out
  // NOT_Gate not_81 has open pins: in=open, out=not_81_out
  // NOT_Gate not_82 has open pins: in=open, out=not_82_out
  or or_13 (or_13_out, not_67_out, not_72_out);
  or or_14 (or_14_out, not_77_out, not_82_out);
  or or_15 (or_15_out, or_13_out, or_14_out);
  // NOT_Gate not_83 has open pins: in=open, out=not_83_out
  // NOT_Gate not_84 has open pins: in=open, out=not_84_out
  // NOT_Gate not_85 has open pins: in=open, out=not_85_out
  // NOT_Gate not_86 has open pins: in=open, out=not_86_out
  // NOT_Gate not_87 has open pins: in=open, out=not_87_out
  // NOT_Gate not_88 has open pins: in=open, out=not_88_out
  // NOT_Gate not_89 has open pins: in=open, out=not_89_out
  // NOT_Gate not_90 has open pins: in=open, out=not_90_out
  // NOT_Gate not_91 has open pins: in=open, out=not_91_out
  // NOT_Gate not_92 has open pins: in=open, out=not_92_out
  // NOT_Gate not_93 has open pins: in=open, out=not_93_out
  // NOT_Gate not_94 has open pins: in=open, out=not_94_out
  // NOT_Gate not_95 has open pins: in=open, out=not_95_out
  // NOT_Gate not_96 has open pins: in=open, out=not_96_out
  // NOT_Gate not_97 has open pins: in=open, out=not_97_out
  // NOT_Gate not_98 has open pins: in=open, out=not_98_out
  or or_16 (or_16_out, not_83_out, not_88_out);
  or or_17 (or_17_out, not_93_out, not_98_out);
  or or_18 (E, or_16_out, or_17_out);
  // NOT_Gate not_99 has open pins: in=open, out=not_99_out
  // NOT_Gate not_100 has open pins: in=open, out=not_100_out
  // NOT_Gate not_101 has open pins: in=open, out=not_101_out
  // NOT_Gate not_102 has open pins: in=open, out=not_102_out
  // NOT_Gate not_103 has open pins: in=open, out=not_103_out
  // NOT_Gate not_104 has open pins: in=open, out=not_104_out
  // NOT_Gate not_105 has open pins: in=open, out=not_105_out
  // NOT_Gate not_106 has open pins: in=open, out=not_106_out
  // NOT_Gate not_107 has open pins: in=open, out=not_107_out
  // NOT_Gate not_108 has open pins: in=open, out=not_108_out
  // NOT_Gate not_109 has open pins: in=open, out=not_109_out
  // NOT_Gate not_110 has open pins: in=open, out=not_110_out
  // NOT_Gate not_111 has open pins: in=open, out=not_111_out
  // NOT_Gate not_112 has open pins: in=open, out=not_112_out
  // NOT_Gate not_113 has open pins: in=open, out=not_113_out
  // NOT_Gate not_114 has open pins: in=open, out=not_114_out
  or or_19 (or_19_out, not_101_out, not_102_out);
  or or_20 (or_20_out, not_99_out, not_100_out);
  or or_21 (or_21_out, or_20_out, or_19_out);
  // NOT_Gate not_115 has open pins: in=open, out=not_115_out
  // NOT_Gate not_116 has open pins: in=open, out=not_116_out
  // NOT_Gate not_117 has open pins: in=open, out=not_117_out
  // NOT_Gate not_118 has open pins: in=open, out=not_118_out
  // NOT_Gate not_119 has open pins: in=open, out=not_119_out
  // NOT_Gate not_120 has open pins: in=open, out=not_120_out
  // NOT_Gate not_121 has open pins: in=open, out=not_121_out
  // NOT_Gate not_122 has open pins: in=open, out=not_122_out
  // NOT_Gate not_123 has open pins: in=open, out=not_123_out
  // NOT_Gate not_124 has open pins: in=open, out=not_124_out
  // NOT_Gate not_125 has open pins: in=open, out=not_125_out
  // NOT_Gate not_126 has open pins: in=open, out=not_126_out
  // NOT_Gate not_127 has open pins: in=open, out=not_127_out
  // NOT_Gate not_128 has open pins: in=open, out=not_128_out
  // NOT_Gate not_129 has open pins: in=open, out=not_129_out
  // NOT_Gate not_130 has open pins: in=open, out=not_130_out
  or or_22 (or_22_out, not_115_out, not_120_out);
  or or_23 (or_23_out, not_125_out, not_130_out);
  or or_24 (or_24_out, or_22_out, or_23_out);
  // NOT_Gate not_131 has open pins: in=open, out=not_131_out
  // NOT_Gate not_132 has open pins: in=open, out=not_132_out
  // NOT_Gate not_133 has open pins: in=open, out=not_133_out
  // NOT_Gate not_134 has open pins: in=open, out=not_134_out
  // NOT_Gate not_135 has open pins: in=open, out=not_135_out
  // NOT_Gate not_136 has open pins: in=open, out=not_136_out
  // NOT_Gate not_137 has open pins: in=open, out=not_137_out
  // NOT_Gate not_138 has open pins: in=open, out=not_138_out
  // NOT_Gate not_139 has open pins: in=open, out=not_139_out
  // NOT_Gate not_140 has open pins: in=open, out=not_140_out
  // NOT_Gate not_141 has open pins: in=open, out=not_141_out
  // NOT_Gate not_142 has open pins: in=open, out=not_142_out
  // NOT_Gate not_143 has open pins: in=open, out=not_143_out
  // NOT_Gate not_144 has open pins: in=open, out=not_144_out
  // NOT_Gate not_145 has open pins: in=open, out=not_145_out
  // NOT_Gate not_146 has open pins: in=open, out=not_146_out
  or or_25 (or_25_out, not_132_out, not_136_out);
  or or_26 (or_26_out, or_25_out, not_135_out);
  or or_27 (or_27_out, not_12_out, not_13_out);
  or or_28 (or_28_out, not_16_out, not_18_out);
  or or_29 (or_29_out, or_27_out, or_28_out);
  or or_30 (or_30_out, not_23_out, not_27_out);
  or or_31 (or_31_out, or_30_out, not_31_out);
  or or_32 (or_32_out, not_40_out, not_45_out);
  or or_33 (or_33_out, or_32_out, or_55_out);
  or or_34 (or_34_out, or_11_out, not_42_out);
  or or_35 (or_35_out, not_53_out, not_56_out);
  or or_36 (or_36_out, or_35_out, not_59_out);
  or or_37 (or_37_out, not_54_out, not_57_out);
  or or_38 (or_38_out, not_67_out, not_72_out);
  or or_39 (or_39_out, not_92_out, not_95_out);
  or or_40 (or_40_out, not_87_out, not_91_out);
  or or_41 (or_41_out, or_40_out, or_39_out);
  or or_42 (or_42_out, not_107_out, not_108_out);
  or or_43 (or_43_out, not_103_out, not_105_out);
  or or_44 (or_44_out, or_43_out, or_42_out);
  or or_45 (or_45_out, or_21_out, or_44_out);
  or or_46 (or_46_out, not_115_out, not_120_out);
  or or_47 (or_47_out, not_134_out, not_137_out);
  or or_48 (or_48_out, or_47_out, not_138_out);
  or or_49 (or_49_out, or_48_out, or_73_out);
  or or_50 (or_50_out, not_133_out, not_139_out);
  or or_51 (or_51_out, or_50_out, not_141_out);
  or or_52 (or_52_out, not_9_out, not_10_out);
  or or_53 (or_53_out, or_52_out, not_17_out);
  or or_54 (or_54_out, not_25_out, not_28_out);
  or or_55 (or_55_out, not_46_out, not_49_out);
  or or_56 (or_56_out, or_33_out, not_50_out);
  or or_57 (or_57_out, not_60_out, not_63_out);
  or or_58 (or_58_out, or_37_out, or_57_out);
  or or_59 (or_59_out, not_77_out, not_82_out);
  or or_60 (or_60_out, or_38_out, or_59_out);
  or or_61 (or_61_out, not_70_out, not_79_out);
  or or_62 (or_62_out, not_84_out, not_85_out);
  or or_63 (or_63_out, not_96_out, not_97_out);
  or or_64 (G, or_41_out, or_63_out);
  or or_65 (or_65_out, not_99_out, not_100_out);
  or or_66 (or_66_out, or_45_out, not_111_out);
  or or_67 (or_67_out, not_125_out, not_130_out);
  or or_68 (or_68_out, or_46_out, or_67_out);
  or or_69 (or_69_out, not_116_out, not_119_out);
  or or_70 (or_70_out, or_69_out, or_95_out);
  or or_71 (or_71_out, not_140_out, not_142_out);
  or or_72 (or_72_out, not_143_out, not_144_out);
  or or_73 (or_73_out, or_71_out, or_72_out);
  or or_74 (or_74_out, or_49_out, or_97_out);
  or or_75 (or_75_out, not_26_out, not_32_out);
  or or_76 (or_76_out, not_30_out, not_33_out);
  or or_77 (or_77_out, not_40_out, not_44_out);
  or or_78 (or_78_out, or_77_out, or_104_out);
  or or_79 (or_79_out, not_58_out, not_61_out);
  or or_80 (or_80_out, or_79_out, not_64_out);
  or or_81 (L5, not_62_out, not_65_out);
  or or_82 (or_82_out, not_75_out, not_80_out);
  or or_83 (or_83_out, not_69_out, not_74_out);
  or or_84 (or_84_out, or_83_out, or_82_out);
  or or_85 (or_85_out, not_90_out, not_94_out);
  or or_86 (or_86_out, not_86_out, not_89_out);
  or or_87 (or_87_out, or_62_out, or_86_out);
  or or_88 (L, or_87_out, or_85_out);
  or or_89 (or_89_out, not_103_out, not_105_out);
  or or_90 (or_90_out, not_101_out, not_102_out);
  or or_91 (or_91_out, or_65_out, or_90_out);
  or or_92 (or_92_out, or_91_out, or_113_out);
  or or_93 (or_93_out, not_117_out, not_122_out);
  or or_94 (or_94_out, or_93_out, or_117_out);
  or or_95 (or_95_out, not_126_out, not_129_out);
  or or_96 (or_96_out, not_132_out, not_133_out);
  or or_97 (or_97_out, not_145_out, not_146_out);
  or or_98 (or_98_out, or_96_out, or_119_out);
  or or_99 (or_99_out, not_6_out, not_8_out);
  or or_100 (or_100_out, not_4_out, not_5_out);
  or or_101 (or_101_out, or_100_out, or_99_out);
  or or_102 (or_102_out, not_19_out, not_20_out);
  or or_103 (or_103_out, not_49_out, not_50_out);
  or or_104 (or_104_out, not_45_out, not_46_out);
  or or_105 (or_105_out, or_78_out, or_103_out);
  or or_106 (or_106_out, not_58_out, not_61_out);
  or or_107 (or_107_out, or_106_out, or_132_out);
  or or_108 (C, or_107_out, or_131_out);
  or or_109 (or_109_out, not_68_out, not_71_out);
  or or_110 (or_110_out, not_73_out, not_76_out);
  or or_111 (or_111_out, or_109_out, or_110_out);
  or or_112 (or_112_out, not_107_out, not_108_out);
  or or_113 (or_113_out, or_89_out, or_112_out);
  or or_114 (or_114_out, or_92_out, not_111_out);
  or or_115 (or_115_out, not_104_out, not_106_out);
  or or_116 (or_116_out, not_118_out, not_121_out);
  or or_117 (or_117_out, not_123_out, not_128_out);
  or or_118 (or_118_out, or_116_out, or_143_out);
  or or_119 (or_119_out, not_135_out, not_136_out);
  or or_120 (or_120_out, not_139_out, not_141_out);
  or or_121 (or_121_out, or_98_out, or_120_out);
  or or_122 (or_122_out, not_16_out, not_18_out);
  or or_123 (or_123_out, not_12_out, not_13_out);
  or or_124 (or_124_out, or_123_out, or_122_out);
  or or_125 (or_125_out, or_101_out, or_124_out);
  or or_126 (or_126_out, not_23_out, not_27_out);
  or or_127 (or_127_out, not_21_out, not_22_out);
  or or_128 (or_128_out, or_102_out, or_127_out);
  or or_129 (or_129_out, or_126_out, not_31_out);
  or or_130 (or_130_out, or_128_out, or_129_out);
  or or_131 (or_131_out, not_65_out, not_66_out);
  or or_132 (or_132_out, not_62_out, not_64_out);
  or or_133 (or_133_out, not_52_out, not_53_out);
  or or_134 (or_134_out, not_78_out, not_81_out);
  or or_135 (or_135_out, or_111_out, or_134_out);
  or or_136 (or_136_out, not_68_out, not_69_out);
  or or_137 (or_137_out, or_136_out, or_153_out);
  or or_138 (or_138_out, or_137_out, or_155_out);
  or or_139 (or_139_out, not_109_out, not_110_out);
  or or_140 (or_140_out, not_112_out, not_113_out);
  or or_141 (or_141_out, or_115_out, or_139_out);
  or or_142 (or_142_out, or_141_out, or_140_out);
  or or_143 (or_143_out, not_124_out, not_127_out);
  or or_144 (or_144_out, not_119_out, not_122_out);
  or or_145 (or_145_out, not_116_out, not_117_out);
  or or_146 (or_146_out, or_145_out, or_144_out);
  or or_147 (or_147_out, not_24_out, not_25_out);
  or or_148 (or_148_out, or_147_out, not_29_out);
  or or_149 (or_149_out, not_58_out, not_59_out);
  or or_150 (or_150_out, not_55_out, not_56_out);
  or or_151 (or_151_out, or_133_out, or_150_out);
  or or_152 (or_152_out, or_151_out, or_166_out);
  or or_153 (or_153_out, not_71_out, not_73_out);
  or or_154 (or_154_out, not_74_out, not_75_out);
  or or_155 (or_155_out, or_154_out, or_168_out);
  or or_156 (or_156_out, not_104_out, not_106_out);
  or or_157 (or_157_out, or_156_out, not_112_out);
  or or_158 (or_158_out, not_128_out, not_129_out);
  or or_159 (or_159_out, not_123_out, not_126_out);
  or or_160 (or_160_out, or_159_out, or_158_out);
  or or_161 (or_161_out, or_146_out, or_160_out);
  or or_162 (or_162_out, not_9_out, not_10_out);
  or or_163 (or_163_out, not_14_out, not_17_out);
  or or_164 (or_164_out, or_162_out, or_163_out);
  or or_165 (or_165_out, not_61_out, not_64_out);
  or or_166 (or_166_out, or_149_out, or_165_out);
  or or_167 (or_167_out, not_80_out, not_81_out);
  or or_168 (or_168_out, not_76_out, not_78_out);
  or or_169 (or_169_out, or_138_out, or_167_out);
  or or_170 (or_170_out, not_109_out, not_110_out);
  or or_171 (or_171_out, or_170_out, not_113_out);
  or or_172 (or_172_out, not_70_out, not_73_out);
  or or_173 (or_173_out, not_68_out, not_69_out);
  or or_174 (or_174_out, or_173_out, or_172_out);
  or or_175 (or_175_out, not_38_out, not_41_out);
  or or_176 (or_176_out, not_36_out, not_37_out);
  or or_177 (or_177_out, or_176_out, or_175_out);
  or or_178 (or_178_out, not_74_out, not_78_out);
  or or_179 (S, or_174_out, or_178_out);
  or or_180 (or_180_out, or_177_out, not_42_out);
  or or_181 (or_181_out, not_131_out, or_68_out);
  or or_182 (or_182_out, or_114_out, or_15_out);
  or or_183 (or_183_out, or_181_out, or_182_out);
  or or_184 (or_184_out, or_130_out, or_125_out);
  or or_185 (or_185_out, not_51_out, or_180_out);
  or or_186 (or_186_out, or_185_out, or_184_out);
  or or_187 (Z, or_183_out, or_186_out);
  or or_188 (or_188_out, or_121_out, or_161_out);
  or or_189 (or_189_out, or_188_out, or_142_out);
  or or_190 (or_190_out, or_148_out, or_164_out);
  or or_191 (or_191_out, or_105_out, or_190_out);
  or or_192 (or_192_out, or_152_out, or_191_out);
  or or_193 (or_193_out, or_189_out, or_169_out);
  or or_194 (P, or_193_out, or_192_out);
  or or_195 (or_195_out, not_131_out, or_24_out);
  or or_196 (or_196_out, or_8_out, or_4_out);
  or or_197 (or_197_out, or_34_out, or_196_out);
  or or_198 (or_198_out, or_195_out, or_66_out);
  or or_199 (or_199_out, or_198_out, or_60_out);
  or or_200 (or_200_out, not_51_out, or_197_out);
  or or_201 (L0, or_199_out, or_200_out);
  or or_202 (or_202_out, or_26_out, or_70_out);
  or or_203 (or_203_out, or_56_out, or_208_out);
  or or_204 (or_204_out, or_202_out, or_157_out);
  or or_205 (or_205_out, or_204_out, or_135_out);
  or or_206 (or_206_out, or_12_out, or_203_out);
  or or_207 (L1, or_205_out, or_206_out);
  or or_208 (or_208_out, not_24_out, or_53_out);
  or or_209 (or_209_out, or_51_out, or_94_out);
  or or_210 (or_210_out, or_209_out, or_171_out);
  or or_211 (or_211_out, or_36_out, or_215_out);
  or or_212 (or_212_out, or_210_out, or_84_out);
  or or_213 (L2, or_212_out, or_211_out);
  or or_214 (or_214_out, or_54_out, not_14_out);
  or or_215 (or_215_out, not_44_out, or_214_out);
  or or_216 (or_216_out, or_74_out, or_118_out);
  or or_217 (or_217_out, or_216_out, not_114_out);
  or or_218 (or_218_out, not_48_out, or_75_out);
  or or_219 (or_219_out, or_58_out, or_218_out);
  or or_220 (or_220_out, or_61_out, or_219_out);
  or or_221 (L3, or_217_out, or_220_out);
  or or_222 (L4, or_80_out, not_29_out);
  or or_223 (L6, not_66_out, or_76_out);

  assign L7 = 1'b0;
  assign L8 = 1'b0;

  // Notes on the sheet:
  //   V
endmodule
